// Logisim project control-logic.circ as structural Verilog: 1 circuit, main circuit control_logic
module control_logic (
  input  [31:0] inst,
  input  BrEq,
  input  BrLt,
  output PCSel,
  output RegWEn,
  output [2:0] ImmSel,
  output BrUn,
  output ASel,
  output BSel,
  output [3:0] ALUSel,
  output MemRW,
  output [1:0] WBSel,
  output CSRSel,
  output CSRWen,
  output [5:0] out_15,
  output [5:0] out_16
);

  wire and_1_out, and_2_out, and_3_out, and_4_out, and_5_out, and_6_out, and_7_out, and_8_out, and_9_out,
       and_10_out, and_11_out, and_12_out, and_13_out, and_14_out, and_15_out, and_16_out, and_17_out,
       and_18_out, and_19_out, and_20_out, and_21_out, and_22_out, and_23_out, and_24_out, and_25_out,
       and_26_out, and_27_out, and_28_out, func3_000, func3_001, func3_010, func3_011, func3_100, func3_101,
       func3_110, func3_111, func7_0b0000000, func7_0b0000001, func7_0b0100000, opcode_0b0010011,
       opcode_0b0010111, opcode_0b0100011, opcode_0b0110011, opcode_0b0110111, opcode_0b1100011,
       opcode_0b1101111, or_1_out;
  wire [2:0] priority_encoder_1_out;
  wire [3:0] priority_encoder_2_out, priority_encoder_3_out;
  wire [5:0] bit_extender_1_out, bit_extender_2_out, bit_extender_3_out;

  Comparator #(.mode("unsigned"), .width(7)) comparator_1 (
    .a(inst[6:0]), .b(7'b0010011), .eq(opcode_0b0010011));  // open: gt, lt
  Comparator #(.mode("unsigned"), .width(7)) comparator_2 (
    .a(inst[6:0]), .b(7'b0110011), .eq(opcode_0b0110011));  // open: gt, lt
  Comparator #(.mode("unsigned"), .width(7)) comparator_3 (
    .a(inst[6:0]), .b(7'b0100011), .eq(opcode_0b0100011));  // open: gt, lt
  Comparator #(.mode("unsigned"), .width(7)) comparator_4 (
    .a(inst[6:0]), .b(7'b1100011), .eq(opcode_0b1100011));  // open: gt, lt
  Comparator #(.mode("unsigned"), .width(7)) comparator_5 (
    .a(inst[6:0]), .b(7'b0010111), .eq(opcode_0b0010111));  // open: gt, lt
  Comparator #(.mode("unsigned"), .width(7)) comparator_6 (
    .a(inst[6:0]), .b(7'b0110111), .eq(opcode_0b0110111));  // open: gt, lt
  Comparator #(.mode("unsigned"), .width(7)) comparator_7 (
    .a(inst[6:0]), .b(7'b1101111), .eq(opcode_0b1101111));  // open: gt, lt
  ROM #(.addrWidth(6), .dataWidth(16)) rom_1 (
    .addr(out_15), .data({RegWEn, ImmSel, BrUn, ASel, BSel, ALUSel, MemRW, WBSel, CSRSel, CSRWen}));
  and and_1 (and_1_out, func3_000, opcode_0b1100011);
  and and_2 (and_2_out, func3_001, opcode_0b1100011);
  and and_3 (and_3_out, func3_100, opcode_0b1100011);
  and and_4 (and_4_out, func3_101, opcode_0b1100011);
  and and_5 (and_5_out, func3_110, opcode_0b1100011);
  and and_6 (and_6_out, func3_111, opcode_0b1100011);
  Priority_Encoder priority_encoder_1 (
    .in0(and_1_out), .in1(and_2_out), .in2(and_3_out), .in3(and_4_out), .in4(and_5_out), .in5(and_6_out),
    .out(priority_encoder_1_out));  // open: in6, in7, en_in, gs, en_out
  Comparator #(.mode("unsigned"), .width(3)) comparator_8 (
    .a(inst[14:12]), .b(3'b000), .eq(func3_000));  // open: gt, lt
  Comparator #(.mode("unsigned"), .width(3)) comparator_9 (
    .a(inst[14:12]), .b(3'b001), .eq(func3_001));  // open: gt, lt
  Comparator #(.mode("unsigned"), .width(3)) comparator_10 (
    .a(inst[14:12]), .b(3'b010), .eq(func3_010));  // open: gt, lt
  Comparator #(.mode("unsigned"), .width(3)) comparator_11 (
    .a(inst[14:12]), .b(3'b011), .eq(func3_011));  // open: gt, lt
  Comparator #(.mode("unsigned"), .width(3)) comparator_12 (
    .a(inst[14:12]), .b(3'b100), .eq(func3_100));  // open: gt, lt
  Comparator #(.mode("unsigned"), .width(3)) comparator_13 (
    .a(inst[14:12]), .b(3'b101), .eq(func3_101));  // open: gt, lt
  Comparator #(.mode("unsigned"), .width(3)) comparator_14 (
    .a(inst[14:12]), .b(3'b110), .eq(func3_110));  // open: gt, lt
  Comparator #(.mode("unsigned"), .width(3)) comparator_15 (
    .a(inst[14:12]), .b(3'b111), .eq(func3_111));  // open: gt, lt
  Comparator #(.mode("unsigned"), .width(7)) comparator_16 (
    .a(inst[31:25]), .b({7{1'b0}}), .eq(func7_0b0000000));  // open: gt, lt
  Comparator #(.mode("unsigned"), .width(7)) comparator_17 (
    .a(inst[31:25]), .b(7'b0000001), .eq(func7_0b0000001));  // open: gt, lt
  Comparator #(.mode("unsigned"), .width(7)) comparator_18 (
    .a(inst[31:25]), .b(7'b0100000), .eq(func7_0b0100000));  // open: gt, lt
  assign bit_extender_1_out = {{3{1'b0}}, priority_encoder_1_out};  // Bit_Extender bit_extender_1
  Adder #(.width(6)) adder_1 (.a(bit_extender_1_out), .b(6'b011010), .out(out_15));  // open: cin, cout
  and and_7 (and_7_out, opcode_0b0010011, func3_000);
  and and_8 (and_8_out, opcode_0b0010011, func3_001);
  and and_9 (and_9_out, opcode_0b0010011, func3_010);
  and and_10 (and_10_out, opcode_0b0010011, func3_100);
  and and_11 (and_11_out, opcode_0b0010011, func3_101);
  and and_12 (and_12_out, opcode_0b0010011, func3_110);
  and and_13 (and_13_out, opcode_0b0010011, func3_111);
  and and_14 (and_14_out, and_8_out, func7_0b0000000);
  and and_15 (and_15_out, func7_0b0000000, and_11_out);
  and and_16 (and_16_out, and_11_out, func7_0b0100000);
  and and_17 (and_17_out, func3_000, func7_0b0000000, opcode_0b0110011);
  and and_18 (and_18_out, func3_000, func7_0b0000001, opcode_0b0110011);
  and and_19 (and_19_out, func3_000, func7_0b0100000, opcode_0b0110011);
  and and_20 (and_20_out, func3_001, func7_0b0000000, opcode_0b0110011);
  and and_21 (and_21_out, func3_001, func7_0b0000001, opcode_0b0110011);
  and and_22 (and_22_out, func3_011, func7_0b0000001, opcode_0b0110011);
  and and_23 (and_23_out, func3_010, func7_0b0000000, opcode_0b0110011);
  and and_24 (and_24_out, func3_100, func7_0b0000000, opcode_0b0110011);
  and and_25 (and_25_out, func3_101, func7_0b0000000, opcode_0b0110011);
  and and_26 (and_26_out, func3_101, func7_0b0100000, opcode_0b0110011);
  and and_27 (and_27_out, func3_110, func7_0b0000000, opcode_0b0110011);
  and and_28 (and_28_out, func3_111, func7_0b0000000, opcode_0b0110011);
  Priority_Encoder #(.select(4)) priority_encoder_2 (
    .in0(and_7_out), .in1(and_14_out), .in2(and_9_out), .in3(and_10_out), .in4(and_15_out), .in5(and_16_out),
    .in6(and_12_out), .in7(and_13_out), .out(priority_encoder_2_out));  // open: in8, in9, in10, in11, in12, in13, in14, in15, gs, en_out, en_in
  Priority_Encoder #(.select(4)) priority_encoder_3 (
    .in0(and_17_out), .in1(and_18_out), .in2(and_19_out), .in3(and_20_out), .in4(and_21_out),
    .in5(and_22_out), .in6(and_23_out), .in7(and_24_out), .in8(and_25_out), .in9(and_26_out),
    .in10(and_27_out), .in11(and_28_out), .out(priority_encoder_3_out));  // open: in12, in13, in14, in15, gs, en_out, en_in
  assign bit_extender_2_out = {{2{1'b0}}, priority_encoder_3_out};  // Bit_Extender bit_extender_2
  or or_1 (or_1_out, opcode_0b0010111, opcode_0b0110111);
  assign bit_extender_3_out = {{2{1'b0}}, priority_encoder_2_out};  // Bit_Extender bit_extender_3
  Adder #(.width(6)) adder_2 (.a(bit_extender_2_out), .b({6{1'b0}}), .out(out_15));  // open: cin, cout
  Priority_Encoder priority_encoder_4 (
    .in1(opcode_0b0010011), .in2(opcode_0b0100011), .in3(opcode_0b1100011), .in4(or_1_out),
    .in5(opcode_0b1101111), .out(ImmSel));  // open: in0, in6, in7, en_in, gs, en_out
  Adder #(.width(6)) adder_3 (.a(bit_extender_3_out), .b(6'b001111), .out(out_15));  // open: cin, cout

  assign out_16 = out_15;

  // Other names for the same wires on the sheet: opcode[6:0] = inst[6:0]; func3[2:0] = inst[14:12];
  //   func7[6:0] = inst[31:25]; ROM_INPUT[5:0] = out_15

  // Notes on the sheet:
  //   INPUTS to your circuit
  //   Connect ROM Input here ->
  //   R type
  //   lui
  //   uj
  //   I type, opcode = 0b0010011
  //   S type
  //   SB type
  //   auipc
  //   SB type
  //   contents of rom_1 (hex, n*v repeats v):
  //   8004 8104 8184 8024 8124 8164 8044 8084 80a4 81a4 80c4 80e4 0 0 0 9204 9224 9244 9284 92a4 93a4 92c4
  //   92e4 0 0 0 4*260c 2e0c 2e0c
  //   ROM FOR CONTROL LOGIC
  //   func3 = 0
  //   func7 = 0
  //   DON'T CHANGE THE LOCATIONS OF THE INPUTS AND OUTPUTS!
  //   OUTPUT from your circuit
  //   CLOSE
  //   WIRE
  //   TO
  //   USE
  //   ROM
  //   Reminder: Use combinational logic for PCSel
  //   I type
  //   R type
  //   I type
  //   S type
  //   SB type
  //   auipc
  //   lui
  //   uj
endmodule
