// Logisim project cpu.circ as structural Verilog: 1 circuit, main circuit cpu
module cpu (
  input  clk,
  input  [31:0] INSTRUCTION,
  input  [31:0] MEM_READ_DATA,
  output [31:0] MEM_WRITE_ADDRESS,
  output [31:0] PROGRAM_COUNTER,
  output [31:0] ra,
  output [31:0] sp,
  output [31:0] t0,
  output [31:0] t1,
  output [31:0] t2,
  output [31:0] s0,
  output [31:0] s1,
  output [31:0] a0,
  output [31:0] tohost,
  output [3:0] MEM_WRITE_ENABLE,
  output [31:0] MEM_WRITE_DATA,
  output [31:0] out_17,
  output [31:0] out_18,
  output [1:0] out_19,
  output [3:0] out_20,
  output [31:0] out_21
);

  wire ASel, BrEq, BrLt, BrUn, BSel, func3_000, func3_001, func3_010, func3_011, func3_100, func3_101,
       func3_110, func3_111, lb, lh, lw, MemRW, opcode_0b0000011, opcode_0b0010011, opcode_0b0010111,
       opcode_0b0100011, opcode_0b0110011, opcode_0b0110111, opcode_0b1100011, opcode_0b1101111, PCSel,
       RegWEn, sb, sh, sw;
  wire [1:0] priority_encoder_1_out, priority_encoder_2_out;
  wire [2:0] control_logic_1_immsel;
  wire [3:0] multiplexer_5_out, multiplexer_6_out, multiplexer_7_out, multiplexer_10_out, multiplexer_11_out;
  wire [5:0] bit_extender_5_out, bit_extender_6_out, ROM_INPUT;
  wire [7:0] multiplexer_8_out;
  wire [15:0] multiplexer_9_out;
  wire [31:0] bit_extender_1_out, bit_extender_2_out, bit_extender_3_out, bit_extender_4_out, MEM_READ_DATA2,
       multiplexer_1_out, multiplexer_2_out, multiplexer_3_out, multiplexer_13_out, PC_Plus4, rs1,
       shifter_1_out, shifter_2_out, shifter_3_out, shifter_4_out, Write_Data;

  Adder #(.width(32)) adder_1 (.a(PROGRAM_COUNTER), .b(32'h4), .out(PC_Plus4));  // open: cin, cout
  Multiplexer #(.enable("false"), .width(32)) multiplexer_1 (
    .in0(PC_Plus4), .in1(MEM_WRITE_ADDRESS), .out(multiplexer_1_out), .sel(PCSel));
  Register #(.width(32)) PC (.D(multiplexer_1_out), .clk(clk), .Q(PROGRAM_COUNTER));  // open: en, clr
  control_logic control_logic_1 (
    .PCSel(PCSel), .RegWEn(RegWEn), .ImmSel(control_logic_1_immsel), .BrUn(BrUn), .ASel(ASel), .BSel(BSel),
    .ALUSel(out_20), .MemRW(MemRW), .WBSel(out_19), .inst(INSTRUCTION), .BrEq(BrEq), .BrLt(BrLt));  // open: CSRWen, out_15, out_16, CSRSel
  regfile regfile_1 (
    .rs1(INSTRUCTION[19:15]), .rs2(INSTRUCTION[24:20]), .rd(INSTRUCTION[11:7]), .Write_Data(Write_Data),
    .RegWEn(RegWEn), .clk(clk), .ra(ra), .sp(sp), .t0(t0), .t1(t1), .t2(t2), .s0(s0), .s1(s1), .a0(a0),
    .Read_Data_1(rs1), .Read_Data_2(out_21));
  imm_gen imm_gen_1 (.inst(INSTRUCTION), .ImmSel(control_logic_1_immsel), .imm(out_18));
  csr csr_1 (.tohost(tohost));  // open: CSR_address, CSR_din, CSR_WE, clk
  branch_comp branch_comp_1 (.rs1(rs1), .rs2(out_21), .BrUn(BrUn), .BrEq(BrEq), .BrLt(BrLt));
  Multiplexer #(.enable("false"), .width(32)) multiplexer_2 (
    .in0(rs1), .in1(PROGRAM_COUNTER), .out(multiplexer_2_out), .sel(ASel));
  Multiplexer #(.enable("false"), .width(32)) multiplexer_3 (
    .in0(out_21), .in1(out_18), .out(multiplexer_3_out), .sel(BSel));
  alu alu_1 (.Result(MEM_WRITE_ADDRESS), .A(multiplexer_2_out), .B(multiplexer_3_out), .ALUSel(out_20));
  Comparator #(.mode("unsigned"), .width(7)) comparator_1 (
    .a(INSTRUCTION[6:0]), .b(7'b0010011), .eq(opcode_0b0010011));  // open: gt, lt
  Comparator #(.mode("unsigned"), .width(7)) comparator_2 (
    .a(INSTRUCTION[6:0]), .b(7'b0110011), .eq(opcode_0b0110011));  // open: gt, lt
  Comparator #(.mode("unsigned"), .width(7)) comparator_3 (
    .a(INSTRUCTION[6:0]), .b(7'b0100011), .eq(opcode_0b0100011));  // open: gt, lt
  Comparator #(.mode("unsigned"), .width(7)) comparator_4 (
    .a(INSTRUCTION[6:0]), .b(7'b1100011), .eq(opcode_0b1100011));  // open: gt, lt
  Comparator #(.mode("unsigned"), .width(7)) comparator_5 (
    .a(INSTRUCTION[6:0]), .b(7'b0010111), .eq(opcode_0b0010111));  // open: gt, lt
  Comparator #(.mode("unsigned"), .width(7)) comparator_6 (
    .a(INSTRUCTION[6:0]), .b(7'b0110111), .eq(opcode_0b0110111));  // open: gt, lt
  Comparator #(.mode("unsigned"), .width(7)) comparator_7 (
    .a(INSTRUCTION[6:0]), .b(7'b1101111), .eq(opcode_0b1101111));  // open: gt, lt
  Multiplexer #(.enable("false"), .select(2), .width(32)) multiplexer_4 (
    .in0(MEM_READ_DATA2), .in1(MEM_WRITE_ADDRESS), .in2(PC_Plus4), .out(Write_Data), .sel(out_19));  // open: in3
  Comparator #(.mode("unsigned"), .width(3)) comparator_8 (
    .a(INSTRUCTION[14:12]), .b(3'b000), .eq(func3_000));  // open: gt, lt
  Comparator #(.mode("unsigned"), .width(3)) comparator_9 (
    .a(INSTRUCTION[14:12]), .b(3'b001), .eq(func3_001));  // open: gt, lt
  Comparator #(.mode("unsigned"), .width(3)) comparator_10 (
    .a(INSTRUCTION[14:12]), .b(3'b010), .eq(func3_010));  // open: gt, lt
  Comparator #(.mode("unsigned"), .width(3)) comparator_11 (
    .a(INSTRUCTION[14:12]), .b(3'b011), .eq(func3_011));  // open: gt, lt
  Comparator #(.mode("unsigned"), .width(3)) comparator_12 (
    .a(INSTRUCTION[14:12]), .b(3'b100), .eq(func3_100));  // open: gt, lt
  Comparator #(.mode("unsigned"), .width(3)) comparator_13 (
    .a(INSTRUCTION[14:12]), .b(3'b101), .eq(func3_101));  // open: gt, lt
  Comparator #(.mode("unsigned"), .width(3)) comparator_14 (
    .a(INSTRUCTION[14:12]), .b(3'b110), .eq(func3_110));  // open: gt, lt
  Comparator #(.mode("unsigned"), .width(3)) comparator_15 (
    .a(INSTRUCTION[14:12]), .b(3'b111), .eq(func3_111));  // open: gt, lt
  Multiplexer #(.enable("false"), .width(4)) multiplexer_5 (
    .in0(4'b0000), .in1(multiplexer_6_out), .out(multiplexer_5_out), .sel(sb));
  Multiplexer #(.enable("false"), .select(2), .width(4)) multiplexer_6 (
    .in0(4'b0001), .in1(4'b0010), .in2(4'b0100), .in3(4'b1000), .out(multiplexer_6_out),
    .sel(MEM_WRITE_ADDRESS[1:0]));
  Comparator #(.mode("unsigned"), .width(7)) comparator_16 (
    .a(INSTRUCTION[6:0]), .b(7'b0000011), .eq(opcode_0b0000011));  // open: gt, lt
  Multiplexer #(.enable("false"), .select(2), .width(4)) multiplexer_7 (
    .in0(4'b0011), .in2(4'b1100), .out(multiplexer_7_out), .sel(MEM_WRITE_ADDRESS[1:0]));  // open: in1, in3
  Multiplexer #(.enable("false"), .select(2), .width(8)) multiplexer_8 (
    .in0(MEM_READ_DATA[7:0]), .in1(MEM_READ_DATA[15:8]), .in2(MEM_READ_DATA[23:16]),
    .in3(MEM_READ_DATA[31:24]), .out(multiplexer_8_out), .sel(MEM_WRITE_ADDRESS[1:0]));
  Multiplexer #(.enable("false"), .select(2), .width(16)) multiplexer_9 (
    .in0(MEM_READ_DATA[15:0]), .in2(MEM_READ_DATA[31:16]), .out(multiplexer_9_out),
    .sel(MEM_WRITE_ADDRESS[1:0]));  // open: in1, in3
  Multiplexer #(.enable("false"), .width(4)) multiplexer_10 (
    .in0(multiplexer_5_out), .in1(multiplexer_7_out), .out(multiplexer_10_out), .sel(sh));
  assign bit_extender_1_out = {{16{1'b0}}, out_21[15:0]};  // Bit_Extender bit_extender_1
  and and_1 (sb, opcode_0b0100011, func3_000);
  and and_2 (sh, opcode_0b0100011, func3_001);
  and and_3 (sw, opcode_0b0100011, func3_010);
  Multiplexer #(.enable("false"), .width(4)) multiplexer_11 (
    .in0(multiplexer_10_out), .in1(4'b1111), .out(multiplexer_11_out), .sel(sw));
  assign bit_extender_2_out = {{24{1'b0}}, out_21[7:0]};  // Bit_Extender bit_extender_2
  Shifter #(.width(32)) shifter_1 (.in(bit_extender_1_out), .\dist (5'b10000), .out(shifter_1_out));
  and and_4 (lb, opcode_0b0000011, func3_000);
  and and_5 (lh, opcode_0b0000011, func3_001);
  and and_6 (lw, opcode_0b0000011, func3_010);
  assign bit_extender_3_out = {{24{multiplexer_8_out[7]}}, multiplexer_8_out};  // Bit_Extender bit_extender_3
  assign bit_extender_4_out = {{16{multiplexer_9_out[15]}}, multiplexer_9_out};  // Bit_Extender bit_extender_4
  Shifter #(.width(32)) shifter_2 (.in(bit_extender_2_out), .\dist (5'b01000), .out(shifter_2_out));
  Shifter #(.width(32)) shifter_3 (.in(bit_extender_2_out), .\dist (5'b10000), .out(shifter_3_out));
  Shifter #(.width(32)) shifter_4 (.in(bit_extender_2_out), .\dist (5'b11000), .out(shifter_4_out));
  Multiplexer #(.enable("false"), .width(32)) multiplexer_12 (
    .in0(multiplexer_13_out), .in1(bit_extender_3_out), .out(MEM_READ_DATA2), .sel(lb));
  Multiplexer #(.enable("false"), .width(32)) multiplexer_13 (
    .in0(MEM_READ_DATA), .in1(bit_extender_4_out), .out(multiplexer_13_out), .sel(lh));
  Multiplexer #(.enable("false"), .width(4)) multiplexer_14 (
    .in0(4'b0000), .in1(multiplexer_11_out), .out(MEM_WRITE_ENABLE), .sel(MemRW));
  Multiplexer #(.enable("false"), .select(4), .width(32)) multiplexer_15 (
    .in0(MEM_READ_DATA), .in1(bit_extender_2_out), .in2(shifter_2_out), .in3(bit_extender_1_out),
    .in4(shifter_3_out), .in8(shifter_4_out), .in12(shifter_1_out), .in15(out_21), .out(MEM_WRITE_DATA),
    .sel(MEM_WRITE_ENABLE));  // open: in5, in6, in7, in9, in10, in11, in13, in14
  Priority_Encoder #(.select(2)) priority_encoder_1 (
    .in0(sb), .in1(sh), .in2(sw), .out(priority_encoder_1_out));  // open: in3, gs, en_out, en_in
  Priority_Encoder #(.select(2)) priority_encoder_2 (
    .in0(lb), .in1(lh), .in2(lw), .out(priority_encoder_2_out));  // open: in3, gs, en_out, en_in
  assign bit_extender_5_out = {{4{1'b0}}, priority_encoder_1_out};  // Bit_Extender bit_extender_5
  assign bit_extender_6_out = {{4{1'b0}}, priority_encoder_2_out};  // Bit_Extender bit_extender_6
  Adder #(.width(6)) adder_2 (.a(bit_extender_5_out), .b(6'b010111), .out(ROM_INPUT));  // open: cin, cout
  Adder #(.width(6)) adder_3 (.a(bit_extender_6_out), .b(6'b001100), .out(ROM_INPUT));  // open: cin, cout

  assign out_17 = MEM_WRITE_ADDRESS;

  // Other names for the same wires on the sheet: ALU_DATA[31:0] = MEM_WRITE_ADDRESS;
  //   LAST_2_BITS[1:0] = MEM_WRITE_ADDRESS[1:0]; opcode[6:0] = INSTRUCTION[6:0]; rd[4:0] = INSTRUCTION[11:7];
  //   func3[2:0] = INSTRUCTION[14:12]; func7[6:0] = INSTRUCTION[31:25]; rs2[31:0] = out_21; WBSel[1:0] = out_19

  // Notes on the sheet:
  //   Output to IMEM
  //   IMEM (do **NOT** move this)
  //   Inputs from IMEM
  //   It is OK to move the PC, RegFile, ALU, MEM, Branch Comp, Imm Gen, and Control Logic to wherever is most convenient for you when constructing your CPU, and to delete this text
  //   Inputs/Outputs for testing. Do **NOT** move these.
  //   ALU
  //   R type
  //   S type
  //   SB type
  //   auipc
  //   lui
  //   uj
  //   I type, opcode = 0b0010011
  //   func3 = 0
  //   Outputs To DMEM
  //   DMEM (do **NOT** move this)
  //   Inputs From DMEM
  //   I type lb, lh, lw
endmodule
