// Logisim project regfile.circ as structural Verilog: 1 circuit, main circuit regfile
module regfile (
  input  [4:0] rs1,
  input  [4:0] rs2,
  input  [4:0] rd,
  input  [31:0] Write_Data,
  input  RegWEn,
  input  clk,
  output [31:0] ra,
  output [31:0] sp,
  output [31:0] t0,
  output [31:0] t1,
  output [31:0] t2,
  output [31:0] s0,
  output [31:0] s1,
  output [31:0] a0,
  output [31:0] Read_Data_1,
  output [31:0] Read_Data_2
);

  wire a0_we, demultiplexer_1_out0, ra_we, s0_we, s1_we, sp_we, t0_we, t1_we, t2_we, x4_we, x20_we, x31_we;
  wire [31:0] x4, x20, x31;

  Register #(.width(32)) register_1 (.D(Write_Data), .en(ra_we), .clk(clk), .Q(ra));  // open: clr
  Register #(.width(32)) register_2 (.D(Write_Data), .en(sp_we), .clk(clk), .Q(sp));  // open: clr
  Register #(.width(32)) register_3 (.D(Write_Data), .en(x4_we), .clk(clk), .Q(x4));  // open: clr
  Register #(.width(32)) register_4 (.D(Write_Data), .en(t0_we), .clk(clk), .Q(t0));  // open: clr
  Register #(.width(32)) register_5 (.D(Write_Data), .en(t1_we), .clk(clk), .Q(t1));  // open: clr
  Register #(.width(32)) register_6 (.D(Write_Data), .en(t2_we), .clk(clk), .Q(t2));  // open: clr
  Register #(.width(32)) register_7 (.D(Write_Data), .en(s0_we), .clk(clk), .Q(s0));  // open: clr
  Multiplexer #(.enable("false"), .select(5), .width(32)) multiplexer_1 (
    .in0({32{1'b0}}), .in1(ra), .in2(sp), .in4(x4), .in5(t0), .in6(t1), .in7(t2), .in8(s0), .in9(s1),
    .in10(a0), .in20(x20), .in31(x31), .out(Read_Data_1), .sel(rs1));  // open: in3, in11, in12, in13, in14, in15, in16, in17, in18, in19, in21, in22, in23, in24, in25, in26, in27, in28, in29, in30
  Register #(.width(32)) register_8 (.D(Write_Data), .en(s1_we), .clk(clk), .Q(s1));  // open: clr
  Register #(.width(32)) register_9 (.D(Write_Data), .en(a0_we), .clk(clk), .Q(a0));  // open: clr
  Register #(.width(32)) register_10 (.D(Write_Data), .en(x20_we), .clk(clk), .Q(x20));  // open: clr
  Register #(.width(32)) register_11 (.D(Write_Data), .en(x31_we), .clk(clk), .Q(x31));  // open: clr
  Multiplexer #(.enable("false"), .select(5), .width(32)) multiplexer_2 (
    .in0({32{1'b0}}), .in1(ra), .in2(sp), .in4(x4), .in5(t0), .in6(t1), .in7(t2), .in8(s0), .in9(s1),
    .in10(a0), .in20(x20), .in31(x31), .out(Read_Data_2), .sel(rs2));  // open: in3, in11, in12, in13, in14, in15, in16, in17, in18, in19, in21, in22, in23, in24, in25, in26, in27, in28, in29, in30
  Demultiplexer #(.enable("false"), .select(5)) demultiplexer_1 (
    .out0(demultiplexer_1_out0), .out1(ra_we), .out2(sp_we), .out4(x4_we), .out5(t0_we), .out6(t1_we),
    .out7(t2_we), .out8(s0_we), .out9(s1_we), .out10(a0_we), .out20(x20_we), .out31(x31_we), .in(RegWEn),
    .sel(rd));  // open: out3, out11, out12, out13, out14, out15, out16, out17, out18, out19, out21, out22, out23, out24, out25, out26, out27, out28, out29, out30

  // Other names for the same wires on the sheet: read_data1[31:0] = Read_Data_1; read_data2[31:0] = Read_Data_2;
  //   read_reg1[4:0] = rs1; read_reg2[4:0] = rs2; write_en = RegWEn; write_reg[4:0] = rd

  // Notes on the sheet:
  //   INPUTS to your circuit
  //   DON'T CHANGE THE LOCATIONS OF THE INPUTS AND OUTPUTS!
  //   These are DEBUG/TEST outputs from your circuit.
  //   OUTPUTS from your circuit
endmodule
